# Fritzing sketch Zug Anschlussplan (saved by Fritzing 0.9.3b)
circuit board: 8.46667cm x 5.64444cm

parts:
  WeMos_D1_Mini1 = WeMos D1 Mini
  Lok_-_Motor = DC Motor
  Part3 = RFID-RC522-v2
  T1 = Basic FET N-Channel [part_number=IRL3803 package="TO220 [THT]"]
  R1 = Resistor [tolerance=±5% resistance=1k package=THT]
  Step_Down_-_LM2596DC = Voltage Regulator LM1117 [package=sot223]
  hc-sr1_-_Ultraschallsensor = hc-sr04
  U1 = 2-Channel 5v Relay Shield [package=relay-2ch5v10a]
  D1 = Rectifier Diode [part_number=1N4007 package="Melf DO-213 AB [SMD]"]
  R2 = Resistor [tolerance=±5% resistance=100k package=THT]
  Gleis_/_Schiene = Power plug
  D2 = Rectifier Diode [part_number=1N4007 package="Melf DO-213 AB [SMD]"]
  C1 = Tantalum Capacitor [capacitance=100nF package="100 mil [THT, tantalum]"]  # not connected

nets:
  N1: WeMos_D1_Mini1.3V3, Part3.3_3V
  5V: WeMos_D1_Mini1.5V, U1.VCC
  N2: WeMos_D1_Mini1.D0, Part3.RST
  N3: WeMos_D1_Mini1.D2, hc-sr1_-_Ultraschallsensor.Echo
  N4: WeMos_D1_Mini1.D3, R1.Pin_0
  N5: WeMos_D1_Mini1.D4, hc-sr1_-_Ultraschallsensor.Trig
  N6: WeMos_D1_Mini1.D5, Part3.SCK
  N7: WeMos_D1_Mini1.D6, Part3.MISO
  N8: WeMos_D1_Mini1.D7, Part3.MOSI
  N9: WeMos_D1_Mini1.D8, Part3.SDA
  N10: WeMos_D1_Mini1.G, U1.GND, R2.Pin_0
  N11: Lok_-_Motor.pin_2, U1.K1-On
  N12: T1.gate, R1.Pin_1
  N13: T1.drain, D1.anode
  N14: Step_Down_-_LM2596DC.ADJ, D2.cathode
  N15: Step_Down_-_LM2596DC.OUT, Gleis_/_Schiene.GND
  N16: U1.IN1, U1.IN2
  N17: Gleis_/_Schiene.VCC, D2.anode

notes:
  5V
  12 - 22 V
  3,3V
  Steuerung Eisenbahn - LOK
  05.10.2017
  .
  GND
  D
  G
  S
  SDA
  RST
  In
  Out

custom parts:
  RFID-RC522-v2: A simple China made RFID-RC522 Reader; do check the pin labels, as this is a MFRC522 based clone.
  2-Channel 5v Relay Shield: 2 Channel 5v Relay Shield w. 2x SPD-06VDC-SD-C
